// Logisim project logisim1.circ as structural Verilog: 2 circuits, main circuit main
module main (
  input  Num1b1,
  input  Num1b2,
  input  Num2b1,
  input  Num2b2,
  output may,
  output men,
  output ig
);

  wire and_1_out, and_2_out, and_3_out, and_4_out, and_5_out, and_6_out, and_7_out, and_8_out, and_9_out,
       and_10_out, not_1_out, not_2_out, not_3_out, not_4_out, not_5_out, not_6_out, not_7_out, not_8_out,
       not_9_out, not_10_out, not_11_out, not_12_out, not_13_out, not_14_out, not_15_out, not_16_out;

  not not_1 (not_1_out, Num2b1);
  and and_1 (and_1_out, Num1b2, not_1_out, not_2_out);
  not not_2 (not_2_out, Num2b2);
  and and_2 (and_2_out, Num1b1, not_3_out);
  not not_3 (not_3_out, Num2b1);
  and and_3 (and_3_out, Num1b1, Num1b2, not_4_out);
  not not_4 (not_4_out, Num2b2);
  not not_5 (not_5_out, Num1b1);
  not not_6 (not_6_out, Num1b2);
  and and_4 (and_4_out, not_5_out, not_6_out, Num2b2);
  not not_7 (not_7_out, Num1b1);
  and and_5 (and_5_out, not_7_out, Num2b1);
  not not_8 (not_8_out, Num1b2);
  and and_6 (and_6_out, not_8_out, Num2b1, Num2b2);
  not not_9 (not_9_out, Num1b1);
  not not_10 (not_10_out, Num1b2);
  not not_11 (not_11_out, Num2b1);
  not not_12 (not_12_out, Num2b2);
  not not_13 (not_13_out, Num1b1);
  not not_14 (not_14_out, Num2b1);
  not not_15 (not_15_out, Num1b2);
  not not_16 (not_16_out, Num2b2);
  or or_1 (may, and_1_out, and_2_out, and_3_out);
  or or_2 (men, and_4_out, and_5_out, and_6_out);
  and and_7 (and_7_out, not_9_out, not_10_out, not_11_out, not_12_out);
  and and_8 (and_8_out, not_13_out, Num1b2, not_14_out, Num2b2);
  and and_9 (and_9_out, Num1b1, not_15_out, Num2b1, not_16_out);
  and and_10 (and_10_out, Num1b1, Num1b2, Num2b1, Num2b2);
  or or_3 (ig, and_7_out, and_8_out, and_9_out, and_10_out);
endmodule

module logisim1 (
  input  Num1b1,
  input  Num1b2,
  input  Num2b1,
  input  Num2b2,
  output may,
  output men,
  output ig
);

  wire and_1_out, and_2_out, and_3_out, and_4_out, and_5_out, and_6_out, and_7_out, and_8_out, and_9_out,
       and_10_out, not_1_out, not_2_out, not_3_out, not_4_out, not_5_out, not_6_out, not_7_out, not_8_out,
       not_9_out, not_10_out, not_11_out, not_12_out, not_13_out, not_14_out, not_15_out, not_16_out;

  not not_1 (not_1_out, Num2b1);
  and and_1 (and_1_out, Num1b2, not_1_out, not_2_out);
  not not_2 (not_2_out, Num2b2);
  and and_2 (and_2_out, Num1b1, not_3_out);
  not not_3 (not_3_out, Num2b1);
  and and_3 (and_3_out, Num1b1, Num1b2, not_4_out);
  not not_4 (not_4_out, Num2b2);
  not not_5 (not_5_out, Num1b1);
  not not_6 (not_6_out, Num1b2);
  and and_4 (and_4_out, not_5_out, not_6_out, Num2b2);
  not not_7 (not_7_out, Num1b1);
  and and_5 (and_5_out, not_7_out, Num2b1);
  not not_8 (not_8_out, Num1b2);
  and and_6 (and_6_out, not_8_out, Num2b1, Num2b2);
  not not_9 (not_9_out, Num1b1);
  not not_10 (not_10_out, Num1b2);
  not not_11 (not_11_out, Num2b1);
  not not_12 (not_12_out, Num2b2);
  not not_13 (not_13_out, Num1b1);
  not not_14 (not_14_out, Num2b1);
  not not_15 (not_15_out, Num1b2);
  not not_16 (not_16_out, Num2b2);
  or or_1 (may, and_1_out, and_2_out, and_3_out);
  or or_2 (men, and_4_out, and_5_out, and_6_out);
  and and_7 (and_7_out, not_9_out, not_10_out, not_11_out, not_12_out);
  and and_8 (and_8_out, not_13_out, Num1b2, not_14_out, Num2b2);
  and and_9 (and_9_out, Num1b1, not_15_out, Num2b1, not_16_out);
  and and_10 (and_10_out, Num1b1, Num1b2, Num2b1, Num2b2);
  or or_3 (ig, and_7_out, and_8_out, and_9_out, and_10_out);
endmodule
